# Fritzing sketch ccs811_promicro (saved by Fritzing 0.9.3b)

parts:
  SparkFun_Pro_Micro1 = SparkFun Pro Micro [part_number=DEV-12640]
  SparkFun_Air_Quality_Breakout_-_CCS1 = SparkFun Air Quality Breakout - CCS811 [part_number="SEN-14193 "]

nets:
  GND: SparkFun_Pro_Micro1.GND, SparkFun_Air_Quality_Breakout_-_CCS1.GND
  VCC: SparkFun_Pro_Micro1.VCC, SparkFun_Air_Quality_Breakout_-_CCS1.3.3V
  N1: SparkFun_Pro_Micro1.D3, SparkFun_Air_Quality_Breakout_-_CCS1.SCL
  N2: SparkFun_Pro_Micro1.D2, SparkFun_Air_Quality_Breakout_-_CCS1.SDA

custom parts:
  SparkFun Pro Micro: This tiny little board does all of the neat-o Arduino tricks that you’re familiar with: 4 channels of 10-bit ADC, 5 PWM pins, 12 DIOs as well as hardware serial connections Rx and Tx. Running at 16MHz and 5V, this board will remind you a lot of your other favorite Arduino-compatible boards but this little guy can go just about anywhere. There is a voltage regulator on board so it can accept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
  SparkFun Air Quality Breakout - CCS811: The CCS811 Air Quality Breakout is a digital gas sensor solution that senses a wide range of Total Volatile Organic Compounds (TVOCs), including equivalent carbon dioxide (eCO2) and metal oxide (MOX) levels. VOCs are often categorized as pollutants and/or sensory irritants and can come from a variety of sources like construction materials (paint, carpet, etc.), machines (copiers, processors,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
